# Fritzing sketch sketch (saved by Fritzing 0.9.0b)
breadboards: 1

parts:
  Arduino = Arduino Mega 2560 (Rev3)
  R1 = Resistor [tolerance=±20% resistance=100k package=THT]
  C1 = Electrolytic Capacitor [capacitance=4.7µF voltage=25V package="100 mil [THT, electrolytic]"]
  R3 = Temperature Sensor (Thermistor) [thermistor_type=NTC part_number=TH1 package=THT]
  R4 = Resistor [tolerance=±5% resistance=220 package=THT]
  R5 = Resistor [tolerance=±5% resistance=1k package=THT]
  Q2 = NPN-Transistor [package="SOT-23 [SMD]"]
  Q1 = Basic FET N-Channel [package="TO220 [THT]"]
  V1 = DC Power [voltage=12V]
  R6 = Resistor [tolerance=±5% resistance=220 part_number=Hotbed package=THT]

nets:
  N1: Arduino.A8, R1.Pin_1, C1.+, R3.pin_0
  N2: Arduino.5V, R3.pin_1, R4.Pin_0
  N3: Arduino.GND, R1.Pin_0, C1.-, Q2.2, Q1.source, V1.V-
  N4: Arduino.VIN, R5.Pin_0, V1.V+, R6.Pin_1
  N5: Arduino.D3_PWM, R4.Pin_1, Q2.0
  N6: R5.Pin_1, Q2.1, Q1.gate
  N7: Q1.drain, R6.Pin_0
